# Fritzing sketch Individual_Hookup_MM8452 (saved by Fritzing 0.9.3b)

parts:
  SparkFun_ESP8266_Thing_-_Dev_Board1 = SparkFun ESP8266 Thing - Dev Board [part_number=WRL-13711]
  3-Axis_Accelerometer2 = 3-Axis Accelerometer Breakout - MMA8452Q

nets:
  GND: SparkFun_ESP8266_Thing_-_Dev_Board1.GND, 3-Axis_Accelerometer2.GND
  VCC: SparkFun_ESP8266_Thing_-_Dev_Board1.VCC, 3-Axis_Accelerometer2.3.3V
  N1: SparkFun_ESP8266_Thing_-_Dev_Board1.GPIO2, 3-Axis_Accelerometer2.SDA
  N2: SparkFun_ESP8266_Thing_-_Dev_Board1.GPIO14, 3-Axis_Accelerometer2.SCL

custom parts:
  SparkFun ESP8266 Thing - Dev Board: This is the SparkFun ESP8266 Thing Dev Board – a development board that has been solely designed around the ESP8266, with an integrated FTDI USB-to-Serial chip. The ESP8266 is a cost-effective, and very capable WiFi-enabled microcontroller. Like any microcontroller, it can be programmed to blink LEDs, trigger relays, monitor sensors, or automate coffee makers, and with an integrated WiFi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
