# Fritzing sketch Individual_Hookup_VCNL4010 (saved by Fritzing 0.9.3b)

parts:
  Part1 = Adafruit VCNL4010 Proximity and Light sensor [part_number="Adafruit #466"]
  SparkFun_ESP8266_Thing_-_Dev_Board1 = SparkFun ESP8266 Thing - Dev Board [part_number=WRL-13711]

nets:
  N1: Part1.SDA, SparkFun_ESP8266_Thing_-_Dev_Board1.GPIO2
  N2: Part1.SCL, SparkFun_ESP8266_Thing_-_Dev_Board1.GPIO14
  GND: Part1.GND, SparkFun_ESP8266_Thing_-_Dev_Board1.GND
  N3: Part1.VIN, SparkFun_ESP8266_Thing_-_Dev_Board1.USBVCC

custom parts:
  Adafruit VCNL4010 Proximity and Light sensor: The VCNL4010 sensor is a nice way to add a small-distance proximity sensor to your microcontroller project. For longer distances (in the range of cm, you can use a SHARP IR distance sensor, but those are only good if the object is over 10 cm away. The VCNL4010 is designed for much shorter distances, no more than 200mm (about 7.5") and under our experimentation we found it worked best at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
  SparkFun ESP8266 Thing - Dev Board: This is the SparkFun ESP8266 Thing Dev Board – a development board that has been solely designed around the ESP8266, with an integrated FTDI USB-to-Serial chip. The ESP8266 is a cost-effective, and very capable WiFi-enabled microcontroller. Like any microcontroller, it can be programmed to blink LEDs, trigger relays, monitor sensors, or automate coffee makers, and with an integrated WiFi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
