# Fritzing sketch V1.0_Breadboard_Hookup (saved by Fritzing 0.9.3b)
breadboards: 1

parts:
  SparkFun_ESP8266_Thing_-_Dev_Board2 = SparkFun ESP8266 Thing - Dev Board [part_number=WRL-13711]
  Part2 = Adafruit VCNL4010 Proximity and Light sensor [part_number="Adafruit #466"]
  3-Axis_Accelerometer3 = 3-Axis Accelerometer Breakout - MMA8452Q

nets:
  VCC: SparkFun_ESP8266_Thing_-_Dev_Board2.VCC, 3-Axis_Accelerometer3.3.3V
  N1: SparkFun_ESP8266_Thing_-_Dev_Board2.GPIO2, Part2.SDA, 3-Axis_Accelerometer3.SDA
  N2: SparkFun_ESP8266_Thing_-_Dev_Board2.GPIO14, Part2.SCL, 3-Axis_Accelerometer3.SCL
  N3: SparkFun_ESP8266_Thing_-_Dev_Board2.USBVCC, Part2.VIN
  GND: Part2.GND, 3-Axis_Accelerometer3.GND

custom parts:
  SparkFun ESP8266 Thing - Dev Board: This is the SparkFun ESP8266 Thing Dev Board – a development board that has been solely designed around the ESP8266, with an integrated FTDI USB-to-Serial chip. The ESP8266 is a cost-effective, and very capable WiFi-enabled microcontroller. Like any microcontroller, it can be programmed to blink LEDs, trigger relays, monitor sensors, or automate coffee makers, and with an integrated WiFi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
  Adafruit VCNL4010 Proximity and Light sensor: The VCNL4010 sensor is a nice way to add a small-distance proximity sensor to your microcontroller project. For longer distances (in the range of cm, you can use a SHARP IR distance sensor, but those are only good if the object is over 10 cm away. The VCNL4010 is designed for much shorter distances, no more than 200mm (about 7.5") and under our experimentation we found it worked best at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
