# Fritzing sketch V2_Hookup (saved by Fritzing 0.9.3b)

parts:
  SparkFun_ESP8266_Thing_-_Dev_Board1 = SparkFun ESP8266 Thing - Dev Board [part_number=WRL-13711]
  3-Axis_Accelerometer2 = 3-Axis Accelerometer Breakout - MMA8452Q
  VCC1 = Battery
  S1 = Pushbutton [package="[SMD]"]
  R1 = Resistor [tolerance=±5% resistance=10k package=THT]

nets:
  GND: SparkFun_ESP8266_Thing_-_Dev_Board1.GND, 3-Axis_Accelerometer2.GND, VCC1.-, R1.Pin_1
  VCC: SparkFun_ESP8266_Thing_-_Dev_Board1.VCC, 3-Axis_Accelerometer2.3.3V
  N1: SparkFun_ESP8266_Thing_-_Dev_Board1.GPIO2, 3-Axis_Accelerometer2.SDA
  N2: SparkFun_ESP8266_Thing_-_Dev_Board1.GPIO14, 3-Axis_Accelerometer2.SCL
  N3: SparkFun_ESP8266_Thing_-_Dev_Board1.USBVCC, SparkFun_ESP8266_Thing_-_Dev_Board1.GPIO4, S1.Pin_3, S1.Pin_4
  N4: SparkFun_ESP8266_Thing_-_Dev_Board1.VIN, VCC1.+
  N5: S1.Pin_1, S1.Pin_2, R1.Pin_0

custom parts:
  SparkFun ESP8266 Thing - Dev Board: This is the SparkFun ESP8266 Thing Dev Board – a development board that has been solely designed around the ESP8266, with an integrated FTDI USB-to-Serial chip. The ESP8266 is a cost-effective, and very capable WiFi-enabled microcontroller. Like any microcontroller, it can be programmed to blink LEDs, trigger relays, monitor sensors, or automate coffee makers, and with an integrated WiFi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
